# Fritzing sketch robot-shield (saved by Fritzing 0.9.3b)
circuit board: 4.42431cm x 3.34011cm
breadboards: 1

parts:
  J1 = Basic Servo
  J2 = Basic Servo
  M2 = DC Motor
  M3 = DC Motor
  Raspberry_Pi1 = Raspberry Pi B rev2
  VCC2 = Battery
  IC1 = L293D [package=THT]
  Part2 = 9 Degrees of Freedom - Sensor Stick

nets:
  GND: J1.gnd, J2.gnd, Raspberry_Pi1.GND, VCC2.-, IC1.0V, Part2.GND
  VCC: J1.vcc, J2.vcc, Raspberry_Pi1.5V, IC1.+V
  N1: J1.pulse, Raspberry_Pi1.GPIO_23
  N2: J2.pulse, Raspberry_Pi1.GPIO_24
  N3: M2.pin_1, IC1.Out_1_(_Controlled_by_Enable_1_)
  N4: M2.pin_2, IC1.Out_2_(_Controlled_by_Enable_1_)
  N5: M3.pin_1, IC1.Out_4_(_Controlled_by_Enable_2_)
  N6: M3.pin_2, IC1.Out_3_(_Controlled_by_Enable_2_)
  3V3: Raspberry_Pi1.3V3, Part2.VCC
  N7: Raspberry_Pi1.GPIO_2, Part2.SCL
  N8: Raspberry_Pi1.GPIO_3, Part2.SDA
  N9: Raspberry_Pi1.GPIO_17, IC1.In_3
  N10: Raspberry_Pi1.GPIO_27, IC1.In_2
  N11: Raspberry_Pi1.GPIO_22, IC1.In_1
  N12: Raspberry_Pi1.GPIO_25, IC1.In_4
  N13: VCC2.+, IC1.+Vmotor
